# Fritzing sketch Circuit Digram (saved by Fritzing 0.9.6b)
breadboards: 1

parts:
  U1 = MAX7219 [package=dil24]
  Disp1 = 20mm 8x8 dot matrix row cathode led display with standard pcb pads
  J1 = STM32 Nucleo boards
  R1 = Resistor [tolerance=±5% resistance=22k package="2010 [SMD]"]

nets:
  N1: U1.DIN, J1.PC12
  N2: U1.DIG0, Disp1.pin_9
  N3: U1.DIG4, Disp1.pin_1
  GND: U1.GND, U1.GND2, J1.GND
  N4: U1.DIG6, Disp1.pin_2
  N5: U1.DIG2, Disp1.pin_8
  N6: U1.DIG3, Disp1.pin_12
  N7: U1.DIG7, Disp1.pin_5
  N8: U1.DIG5, Disp1.pin_7
  N9: U1.DIG1, Disp1.pin_14
  N10: U1.LOAD, J1.PA6
  N11: U1.CLK, J1.PC10
  N12: U1.SEGA, Disp1.pin_13
  N13: U1.SEGF, Disp1.pin_11
  N14: U1.SEGB, Disp1.pin_3
  N15: U1.SEGG, Disp1.pin_15
  N16: U1.ISET, R1.Pin_0
  VCC: U1.VCC, J1.5V, R1.Pin_1
  N17: U1.SEGC, Disp1.pin_4
  N18: U1.SEGE, Disp1.pin_6
  N19: U1.SEGDP, Disp1.pin_16
  N20: U1.SEGD, Disp1.pin_10

notes:
  CS
  CK
  MOSI
  MAX7291
